# Fritzing sketch wiring (saved by Fritzing 0.9.3b)

parts:
  Part1 = Arduino Nano (Rev3.0)
  R1 = Resistor [tolerance=±5% resistance=220 package=THT]
  LED-R = LED - 3mm [color="Red (633nm)" package="3 mm [THT]"]
  R2 = Resistor [tolerance=±5% resistance=220 package=THT]
  LED-S = LED - 3mm [color="Red (633nm)" package="3 mm [THT]"]
  SW-S = Pushbutton [package="[SMD]"]
  SW-R = Pushbutton [package="[SMD]"]
  NRF24L1 = NRF24L01
  C1 = Ceramic Capacitor [capacitance=10nF package="0805 [SMD, multilayer]"]
  C2 = Electrolytic Capacitor [capacitance=1000µF package="300 mil [THT, electrolytic]"]
  SW-RST = Pushbutton [package="[SMD]"]
  SSR = RELAY-SOLIDSTATE [package=relay-s108t02]  # not connected
  J1a = female pin header, 8 pins [form="♀ (female)"]
  J1b = female pin header, 8 pins [form="♀ (female)"]
  F1 = FUSE [package=fuse_5mm]  # not connected
  J-S1 = female pin header, 3 pins [form="♀ (female)"]
  J-S2 = female pin header, 3 pins [form="♀ (female)"]
  J-S3 = female pin header, 3 pins [form="♀ (female)"]
  J-SSR-1 = female pin header, 2 pins [form="♀ (female)"]
  J-PSU-5 = female pin header, 2 pins [form="♀ (female)"]
  J-Fuse = rounded female pin header, 2 pins [form="♀ (female rounded)"]
  J220-In = Camdenboss CTB0158-2 [part_number=. package=THT]
  J-SSR-2 = rounded female pin header, 2 pins [form="♀ (female rounded)"]
  J220-Out = Camdenboss CTB0158-2 [part_number=. package=THT]
  J-Earth = Camdenboss CTB0158-2 [part_number=. package=THT]
  J-PSU-220 = rounded female alternating pin header, 3 pins [form="♀ (female rounded)"]
  P1 = Rotary Potentiometer (Small) [maximum_resistance=10kΩ package=THT]
  R5 = Resistor [tolerance=±5% resistance=330 package=THT]

nets (from the breadboard view):
  N1: Part1.RESET, J1a.pin1
  GND: Part1.GND, NRF24L1.GND, C1.0, C2.-, J1a.pin2, J-S1.pin1, J-S2.pin1, J-S3.pin1, J-SSR-1.pin1, J-PSU-5.pin2
  N2: Part1.D5, R1.Pin_1
  N3: Part1.D6, R2.Pin_1
  N4: Part1.D7, J1a.pin5
  N5: Part1.D8, J1a.pin6
  N6: Part1.D9, NRF24L1.CE
  N7: Part1.D10, NRF24L1.CSN
  N8: Part1.D11/MOSI, NRF24L1.MOSI
  N9: Part1.D12/MISO, NRF24L1.MISO
  N10: Part1.5V, C2.+, J1a.pin8, J-S1.pin3, J-S2.pin3, J-S3.pin3, J-PSU-5.pin1
  N11: Part1.A3, R5.Pin_1
  N12: Part1.A2, J-SSR-1.pin2
  N13: Part1.A0, C1.1, J1a.pin7
  3V3: Part1.3V3, NRF24L1.VCC
  N14: Part1.D13/SCK, NRF24L1.SCK
  N15: R1.Pin_0, J1a.pin3
  N16: LED-R.cathode, LED-S.cathode, SW-R.Pin_3, SW-R.Pin_4
  N17: LED-R.anode, J1b.pin4
  N18: R2.Pin_0, J1a.pin4
  N19: LED-S.anode, J1b.pin3
  N20: SW-S.Pin_1, SW-S.Pin_2, J1b.pin6
  N21: SW-S.Pin_3, SW-S.Pin_4, SW-RST.Pin_1, SW-RST.Pin_2, J1b.pin2, P1.leg1
  N22: SW-R.Pin_1, SW-R.Pin_2, J1b.pin5
  N23: SW-RST.Pin_3, J1b.pin1
  N24: J1b.pin7, P1.wiper
  N25: J1b.pin8, P1.leg2
  N26: J-S1.pin2, J-S2.pin2, J-S3.pin2, R5.Pin_0
  N27: J-Fuse.pin1, J220-In.terminal_1
  N28: J-Fuse.pin2, J-SSR-2.pin1, J-PSU-220.pin1
  N29: J220-In.terminal_2, J220-Out.terminal_1, J-PSU-220.pin2
  N30: J-SSR-2.pin2, J220-Out.terminal_2
  N31: J-Earth.terminal_1, J-Earth.terminal_2, J-PSU-220.pin3

custom parts:
  NRF24L01: NRF24L01 module
